# Fritzing sketch board_schematic (saved by Fritzing 0.9.3b)
breadboards: 1

parts:
  Part1 = Arduino Ethernet Shield (Rev3)
  R1 = Resistor [tolerance=±5% resistance=1k package="0402 [SMD]"]
  J1 = Basic Force Sensing Resistor (FSR) [package=THT]
  R2 = Textile Stretch Sensor [part_number=PW052]
  R3 = Resistor [tolerance=±5% resistance=1k package="0402 [SMD]"]
  R4 = Resistor [tolerance=±5% resistance=1k package="0402 [SMD]"]

nets:
  N1: Part1.A0, R2.pin_0, R4.Pin_0
  N2: Part1.A5/SCL, R1.Pin_1, J1.pin_1
  N3: Part1.5V, J1.pin_0, R3.Pin_1
  N4: Part1.GND, R1.Pin_0, R2.pin_1
  N5: R3.Pin_0, R4.Pin_1
